// Logisim project main.circ as structural Verilog: 16 circuits, main circuit main
module main (
  input  S3,
  input  S2,
  input  S1,
  input  S0,
  input  in_5
);

  wire clock_1_out, decodificador_1_p5, decodificador_1_p6, decodificador_1_p7, decodificador_1_p8,
       decodificador_1_p9, decodificador_1_p10, decodificador_1_p11, detectorf_1_f;
  wire [3:0] Estado_Siguiente_out_8, EstadoActual_q0, multiplexer_1_out, multiplexer_2_out;

  Multiplexer #(.enable("true"), .width(4)) multiplexer_1 (
    .in0({S3, S2, S1, S0}), .in1(multiplexer_2_out), .out(multiplexer_1_out), .sel(in_5));  // open: en
  Clock clock_1 (.out(clock_1_out));
  estadoguardado EstadoActual (
    .D3(multiplexer_1_out[3]), .D2(multiplexer_1_out[2]), .D1(multiplexer_1_out[1]),
    .D0(multiplexer_1_out[0]), .CLK(clock_1_out), .Q3(EstadoActual_q0[3]), .Q2(EstadoActual_q0[2]),
    .Q1(EstadoActual_q0[1]), .Q0(EstadoActual_q0[0]));
  Multiplexer #(.enable("true"), .width(4)) multiplexer_2 (
    .in0(Estado_Siguiente_out_8), .in1(EstadoActual_q0), .out(multiplexer_2_out), .sel(detectorf_1_f));  // open: en
  detectorF detectorf_1 (
    .Q3(EstadoActual_q0[3]), .Q2(EstadoActual_q0[2]), .Q1(EstadoActual_q0[1]), .Q0(EstadoActual_q0[0]),
    .F(detectorf_1_f));
  estadosig Estado_Siguiente (
    .Q3(EstadoActual_q0[3]), .Q2(EstadoActual_q0[2]), .Q1(EstadoActual_q0[1]), .Q0(EstadoActual_q0[0]),
    .out_6(Estado_Siguiente_out_8[2]), .out_7(Estado_Siguiente_out_8[1]), .out_8(Estado_Siguiente_out_8[0]),
    .out_5(Estado_Siguiente_out_8[3]));
  // decodificador decodificador_1: pin names not known; wires that end beside it: Estado_Siguiente_out_8[3], Estado_Siguiente_out_8[2], Estado_Siguiente_out_8[1], Estado_Siguiente_out_8[0], decodificador_1_p5, decodificador_1_p6, decodificador_1_p7, decodificador_1_p8, decodificador_1_p9, decodificador_1_p10, decodificador_1_p11
  _7_Segment_Display u_7_segment_display_1 (
    .g(decodificador_1_p5), .f(decodificador_1_p7), .a(decodificador_1_p9), .b(decodificador_1_p10),
    .e(decodificador_1_p6), .d(decodificador_1_p8), .c(decodificador_1_p11));  // open: dp
endmodule

module decodificador (
  input  A3,
  input  A2,
  input  A1,
  input  A0,
  output out_5,
  output out_6,
  output out_7,
  output out_8,
  output out_9,
  output out_10,
  output out_11
);

  E e_1 (.A0(A0), .A1(A1), .A2(A2), .A3(A3), .out_5(out_9));
  A a_1 (.A0(A0), .A1(A1), .A2(A2), .A3(A3), .out_5(out_5));
  F f_1 (.A0(A0), .A1(A1), .A2(A2), .A3(A3), .out_5(out_10));
  B b_1 (.A0(A0), .A1(A1), .A2(A2), .A3(A3), .out_5(out_6));
  G g_1 (.A0(A0), .A1(A1), .A2(A2), .A3(A3), .out_5(out_11));
  C c_1 (.A0(A0), .A1(A1), .A2(A2), .A3(A3), .out_5(out_7));
  D d_1 (.A0(A0), .A1(A1), .A2(A2), .A3(A3), .out_5(out_8));
endmodule

module D3 (
  input  Q3,
  input  Q2,
  input  Q1,
  input  Q0,
  output out_5
);

  wire and_1_out, and_2_out, nand_1_out, not_1_out;

  not not_1 (not_1_out, Q3);
  nand nand_1 (nand_1_out, Q2, Q1);
  and and_1 (and_1_out, Q3, nand_1_out);
  and and_2 (and_2_out, not_1_out, Q1, Q0);
  or or_1 (out_5, and_1_out, and_2_out);
endmodule

module D2 (
  input  Q3,
  input  Q2,
  input  Q1,
  input  Q0,
  output out_5
);

  wire and_1_out, and_2_out, and_3_out, and_4_out, and_5_out;

  and and_1 (and_1_out, Q3, Q2);
  and and_2 (and_2_out, Q2, Q1);
  and and_3 (and_3_out, Q3, Q1);
  and and_4 (and_4_out, Q2, Q0);
  and and_5 (and_5_out, Q3, Q0);
  or or_1 (out_5, and_1_out, and_5_out);
endmodule

module D1 (
  input  Q3,
  input  Q2,
  input  Q1,
  input  Q0,
  output out_5
);

  wire and_1_out, and_2_out, and_3_out, nor_1_out, nor_2_out, nor_3_out, not_1_out, or_1_out;

  not not_1 (not_1_out, Q1);
  nor nor_1 (nor_1_out, Q3, Q0);
  and and_1 (and_1_out, not_1_out, Q3);
  nor nor_2 (nor_2_out, Q1, Q0);
  nor nor_3 (nor_3_out, Q3, Q1, Q2);
  or or_1 (or_1_out, nor_1_out, and_1_out, nor_2_out);
  and and_2 (and_2_out, or_1_out, Q2);
  and and_3 (and_3_out, nor_3_out, Q0);
  or or_2 (out_5, and_2_out, and_3_out);
endmodule

module D0 (
  input  Q3,
  input  Q2,
  input  Q1,
  input  Q0,
  output out_5
);

  wire and_1_out, and_2_out, nor_1_out, not_1_out, not_2_out, xnor_1_out;

  not not_1 (not_1_out, Q0);
  not not_2 (not_2_out, Q1);
  xnor xnor_1 (xnor_1_out, Q3, Q1);
  nor nor_1 (nor_1_out, Q2, Q1, Q0);
  and and_1 (and_1_out, not_1_out, Q1);
  and and_2 (and_2_out, Q2, not_2_out, Q0);
  or or_1 (out_5, xnor_1_out, nor_1_out, and_1_out, and_2_out);
endmodule

module estadosig (
  input  Q3,
  input  Q2,
  input  Q1,
  input  Q0,
  output out_5,
  output out_6,
  output out_7,
  output out_8
);

  D3 d3_1 (.Q2(Q2), .Q1(Q1), .Q0(Q0), .Q3(Q3), .out_5(out_5));
  D2 d2_1 (.Q2(Q2), .Q1(Q1), .Q0(Q0), .Q3(Q3), .out_5(out_6));
  D1 d1_1 (.Q3(Q3), .Q2(Q2), .Q1(Q1), .Q0(Q0), .out_5(out_7));
  D0 d0_1 (.Q2(Q2), .Q1(Q1), .Q0(Q0), .Q3(Q3), .out_5(out_8));
endmodule

module estadoguardado (
  input  CLK,
  input  D3,
  input  D2,
  input  D1,
  input  D0,
  output Q3,
  output Q2,
  output Q1,
  output Q0
);

  wire undriven, undriven_2, undriven_3;

  D_Flip_Flop d_ff_1 (.D(CLK), .clk(D3), .Q(Q3), .preset(undriven));  // open: Qn, reset
  D_Flip_Flop d_ff_2 (.D(CLK), .clk(D2), .Q(Q2), .preset(undriven_2));  // open: Qn, reset
  D_Flip_Flop d_ff_3 (.D(CLK), .clk(D1), .Q(Q1), .reset(undriven_3));  // open: Qn, preset
  D_Flip_Flop d_ff_4 (.D(CLK), .clk(D0), .Q(Q0));  // open: Qn, preset, reset
endmodule

module detectorF (
  input  Q3,
  input  Q2,
  input  Q1,
  input  Q0,
  output F
);

  wire not_1_out, not_2_out;

  not not_1 (not_1_out, Q3);
  not not_2 (not_2_out, Q1);
  and and_1 (F, not_1_out, Q2, not_2_out, Q0);
endmodule

module A (
  input  A0,
  input  A1,
  input  A2,
  input  A3,
  output out_5
);

  wire and_1_out, and_2_out, nor_1_out, not_1_out, or_1_out, or_2_out;

  or or_1 (or_1_out, A0, A1);
  not not_1 (not_1_out, A0);
  or or_2 (or_2_out, not_1_out, A1);
  nor nor_1 (nor_1_out, A0, A1, A3);
  and and_1 (and_1_out, or_1_out, A3);
  and and_2 (and_2_out, A2, or_2_out);
  or or_3 (out_5, nor_1_out, and_1_out, and_2_out);
endmodule

module B (
  input  A0,
  input  A1,
  input  A2,
  input  A3,
  output out_5
);

  wire and_1_out, and_2_out, and_3_out, nor_1_out, not_1_out, not_2_out, not_3_out, or_1_out;

  not not_1 (not_1_out, A2);
  not not_2 (not_2_out, A1);
  nor nor_1 (nor_1_out, A0, A2);
  and and_1 (and_1_out, nor_1_out, A1);
  or or_1 (or_1_out, A1, not_1_out);
  and and_2 (and_2_out, or_1_out, not_3_out);
  not not_3 (not_3_out, A3);
  and and_3 (and_3_out, A3, not_2_out, A0);
  or or_2 (out_5, and_1_out, and_2_out, and_3_out);
endmodule

module C (
  input  A0,
  input  A1,
  input  A2,
  input  A3,
  output out_5
);

  wire and_1_out, and_2_out, and_3_out, nor_1_out, not_1_out, not_2_out;

  nor nor_1 (nor_1_out, A0, A1);
  not not_1 (not_1_out, A3);
  and and_1 (and_1_out, nor_1_out, A3);
  not not_2 (not_2_out, A2);
  and and_2 (and_2_out, A2, not_1_out);
  and and_3 (and_3_out, A0, not_2_out);
  or or_1 (out_5, and_1_out, and_3_out, and_2_out);
endmodule

module D (
  input  A0,
  input  A1,
  input  A2,
  input  A3,
  output out_5
);

  wire and_1_out, and_2_out, and_3_out, and_4_out, and_5_out, not_1_out, not_2_out, not_3_out, not_4_out,
       or_1_out, or_2_out;

  not not_1 (not_1_out, A0);
  not not_2 (not_2_out, A1);
  not not_3 (not_3_out, A2);
  not not_4 (not_4_out, A3);
  or or_1 (or_1_out, A0, not_2_out, not_4_out);
  and and_1 (and_1_out, A0, not_4_out);
  and and_2 (and_2_out, not_1_out, not_3_out, A3);
  or or_2 (or_2_out, and_1_out, and_2_out);
  and and_3 (and_3_out, or_1_out, A2);
  and and_4 (and_4_out, A1, or_2_out);
  and and_5 (and_5_out, not_1_out, not_2_out, not_4_out);
  or or_3 (out_5, and_3_out, and_4_out, and_5_out);
endmodule

module E (
  input  A0,
  input  A1,
  input  A2,
  input  A3,
  output out_5
);

  wire and_1_out, and_2_out, and_3_out, and_4_out, and_5_out, not_1_out, not_2_out, not_3_out, not_4_out,
       or_1_out, or_2_out;

  not not_1 (not_1_out, A0);
  not not_2 (not_2_out, A1);
  not not_3 (not_3_out, A2);
  not not_4 (not_4_out, A3);
  and and_1 (and_1_out, A1, A2);
  and and_2 (and_2_out, not_3_out, not_4_out);
  or or_1 (or_1_out, not_2_out, A3);
  or or_2 (or_2_out, and_1_out, and_2_out);
  and and_3 (and_3_out, A0, or_1_out);
  and and_4 (and_4_out, not_1_out, or_2_out);
  and and_5 (and_5_out, A2, A3);
  or or_3 (out_5, and_3_out, and_4_out, and_5_out);
endmodule

module F (
  input  A0,
  input  A1,
  input  A2,
  input  A3,
  output out_5
);

  wire xor_1_out, xor_2_out;

  xor xor_1 (xor_1_out, A0, A3);
  xor xor_2 (xor_2_out, A1, A2);
  or or_1 (out_5, xor_1_out, xor_2_out);
endmodule

module G (
  input  A0,
  input  A1,
  input  A2,
  input  A3,
  output out_5
);

  wire and_1_out, and_2_out, nor_1_out, nor_2_out, not_1_out, or_1_out;

  nor nor_1 (nor_1_out, A0, A2);
  nor nor_2 (nor_2_out, A1, A3);
  and and_1 (and_1_out, nor_1_out, A1);
  not not_1 (not_1_out, A1);
  or or_1 (or_1_out, not_1_out, A2, A3);
  and and_2 (and_2_out, A0, or_1_out);
  or or_2 (out_5, and_1_out, and_2_out, nor_2_out);
endmodule
